# Fritzing sketch WeightScale (saved by Fritzing 0.8.5b)
breadboards: 1
perfboards: 2

parts:
  J1 = female pin header, 4 pins [form="♀ (female)"]
  J3 = female pin header, 4 pins [form="♀ (female)"]  # not connected
  J4 = female pin header, 3 pins [form="♀ (female)"]
  R2 = Resistor [tolerance=±0.1% resistance=1k package=THT]
  R3 = Resistor [tolerance=±0.1% resistance=1k package=THT]
  R1 = Resistor [tolerance=±0.1% resistance=1k package=THT]
  J2 = female pin header, 4 pins [form="♀ (female)"]
  R4 = Resistor [tolerance=±0.1% resistance=1k package=THT]
  J5 = female pin header, 3 pins [form="♀ (female)"]
  J6 = female pin header, 4 pins [form="♀ (female)"]
  J7 = female pin header, 4 pins [form="♀ (female)"]
  J8 = female pin header, 4 pins [form="♀ (female)"]  # not connected

nets:
  N1: J1.pin1, J4.pin1, R1.Pin_0, J2.pin1
  N2: J1.pin2, J4.pin2, R2.Pin_1, J2.pin2
  N3: J1.pin3, J4.pin3, J2.pin3
  N4: J1.pin4, R2.Pin_0, R1.Pin_1, J2.pin4
  N5: R3.Pin_0, J5.pin1
  N6: R3.Pin_1, R4.Pin_0
  N7: R4.Pin_1, J5.pin2
  N8: J6.pin1, J7.pin1
  N9: J6.pin2, J7.pin2
  N10: J6.pin3, J7.pin3
  N11: J6.pin4, J7.pin4

notes:
  HX711
